# Fritzing sketch collision_detection_schematic (saved by Fritzing 0.9.3b)
breadboards: 1

parts:
  Part1 = Photon
  R1 = Resistor [tolerance=±5% resistance=1k package="2010 [SMD]"]
  R2 = Resistor [tolerance=±5% resistance=1k package="0805 [SMD]"]
  R3 = Resistor [tolerance=±5% resistance=1k package="0603 [SMD]"]  # not connected
  R4 = Resistor [tolerance=±5% resistance=1k package="2512 [SMD]"]
  D2 = Diode [package=diode-1n4001]
  U1 = LIPO-110mAh [package=lipo-110]
  M1 = DC Motor
  Q1 = npn-Powertransistor [package="TO220 [THT]"]
  J1 = Infrared Proximity Sensor
  LED1 = RGB LED (com. cathode, rbg) [package="5 mm [THT]"]

nets (from the breadboard view):
  N1: Part1.A0, J1.Vout
  GND: Part1.GND, D2.A, U1.+, Q1.emitter, J1.GND, LED1.common_cathode
  VIN: Part1.VIN, J1.Vcc
  N2: Part1.D0, R1.Pin_0
  N3: Part1.D1, R2.Pin_0
  N4: Part1.D3, R4.Pin_0
  N5: Part1.3V3, U1.-, M1.pin_2
  N6: R1.Pin_1, LED1.red_anode
  N7: R2.Pin_1, LED1.blue_anode
  N8: R4.Pin_1, Q1.base
  N9: D2.C, M1.pin_1, Q1.collector
